# Fritzing sketch ENGR101FinalProjectCircuit (saved by Fritzing 0.9.9b)
breadboards: 1

parts:
  Part1 = Arduino Mega 2560 (Rev3)
  M1 = Dagu DGServo 9g (Pan and tilt) [part_number=RS001B]
  U1 = LCD-16X2 [package=lcd-16x2]
  PIR1 = PIR sensor

nets:
  N1: Part1.D13_PWM, M1.pulse
  N2: Part1.D12_PWM, U1.DB7
  N3: Part1.D11_PWM, U1.DB6
  N4: Part1.D10_PWM, U1.DB5
  N5: Part1.D9_PWM, U1.DB4
  N6: Part1.D8_PWM, U1.E
  5V: Part1.5V, M1.vcc
  N7: Part1.D5_PWM, PIR1.SIG
  N8: Part1.D7_PWM, U1.RS
  VDD: U1.VDD, U1.A, PIR1.VDD
  N9: U1.R_W, U1.K, PIR1.GND
